# Fritzing sketch maups (saved by Fritzing 0.8.7b)
circuit board: 6.88566cm x 5.36311cm

parts:
  Part1 = Arduino Uno (Rev3)
  Pololu_X = Pololu A4988 [package=SO16]
  X_MOT = female pin header, 4 pins [form="♀ (female)"]
  MS_X = double row female pin header, 6 pins [form="♀ (female)"]
  Pololu_Y = Pololu A4988 [package=SO16]
  Y_MOT = female pin header, 4 pins [form="♀ (female)"]
  MS_Y = double row female pin header, 6 pins [form="♀ (female)"]
  C1 = Electrolytic Capacitor [capacitance=100nF voltage=16V package="100 mil [THT, electrolytic]"]
  C2 = Electrolytic Capacitor [capacitance=100nF voltage=16V package="100 mil [THT, electrolytic]"]
  R1 = Resistor [tolerance=±5% resistance=10k package=THT]
  X_ENDSTOP = female pin header, 2 pins [form="♀ (female)"]
  Y_ENDSTOP = female pin header, 2 pins [form="♀ (female)"]
  U1 = Voltage Regulator [package=to220-adj]
  R2 = Resistor [tolerance=±5% resistance=10 package=THT]
  R3 = Resistor [tolerance=±5% resistance=10 package=THT]
  R4 = Resistor [tolerance=±5% resistance=10 package=THT]
  R5 = Resistor [tolerance=±5% resistance=10 package=THT]
  D1 = Rectifier Diode [part_number=1N4001 package="300 mil [THT]"]
  C3 = Electrolytic Capacitor [capacitance=10µF package="100 mil [THT, electrolytic]"]
  R6 = Trimmer Potentiometer [maximum_resistance=100Ω package=THT]
  LASER = Screw terminal - 2 pins [package=THT]
  Q1 = MOSFET-NCHANNEL [package=to220v]
  R7 = Resistor [tolerance=±5% resistance=10 package=THT]
  R8 = Resistor [tolerance=±5% resistance=100k package=THT]
  Q2 = MOSFET-NCHANNEL [package=to220v]
  R9 = Resistor [tolerance=±5% resistance=10 package=THT]
  R10 = Resistor [tolerance=±5% resistance=100k package=THT]
  FAN = Screw terminal - 2 pins [package=THT]

nets:
  N1: Part1.A3, R9.Pin_1, R10.Pin_1
  N2: Part1.D8, Pololu_X.ENABLE, Pololu_Y.ENABLE, R1.Pin_1
  N3: Part1.D9_PWM, X_ENDSTOP.pin1
  N4: Part1.D10_PWM/SS, Y_ENDSTOP.pin1
  N5: Part1.D12/MISO, R7.Pin_1, R8.Pin_1
  GND: Part1.GND, Pololu_X.GND, Pololu_Y.GND, C1.-, C2.-, X_ENDSTOP.pin2, Y_ENDSTOP.pin2, Q1.S, R8.Pin_0
  N6: Part1.D2, Pololu_X.STEP
  N7: Part1.D3_PWM, Pololu_Y.STEP
  N8: Part1.D5_PWM, Pololu_X.DIR
  N9: Part1.D6_PWM, Pololu_Y.DIR
  VDD: Part1.5V, Pololu_X.VDD, MS_X.pin1, MS_X.pin2, MS_X.pin3, Pololu_Y.VDD, MS_Y.pin1, MS_Y.pin2, MS_Y.pin3, R1.Pin_0
  N10: Part1.VIN, Pololu_X.VMOT, Pololu_Y.VMOT, C1.+, C2.+, U1.IN, FAN.pin2
  N11: Pololu_X.MS1, MS_X.pin4
  N12: Pololu_X.MS2, MS_X.pin5
  N13: Pololu_X.MS3, MS_X.pin6
  N14: Pololu_X.RESET, Pololu_X.SLEEP
  N15: Pololu_X.1B, X_MOT.pin4
  N16: Pololu_X.1A, X_MOT.pin3
  N17: Pololu_X.2A, X_MOT.pin2
  N18: Pololu_X.2B, X_MOT.pin1
  N19: Pololu_Y.MS1, MS_Y.pin4
  N20: Pololu_Y.MS2, MS_Y.pin5
  N21: Pololu_Y.MS3, MS_Y.pin6
  N22: Pololu_Y.RESET, Pololu_Y.SLEEP
  N23: Pololu_Y.1B, Y_MOT.pin4
  N24: Pololu_Y.1A, Y_MOT.pin3
  N25: Pololu_Y.2A, Y_MOT.pin2
  N26: Pololu_Y.2B, Y_MOT.pin1
  N27: U1.ADJ, R6.leg2
  N28: U1.OUT, R2.Pin_0, R3.Pin_0, R4.Pin_0, R5.Pin_0, D1.anode, C3.+, LASER.pin2
  N29: R2.Pin_1, R3.Pin_1, R4.Pin_1, R5.Pin_1, R6.wiper
  N30: D1.cathode, C3.-, LASER.pin1, Q1.D
  N31: Q1.G, R7.Pin_0
  N32: Q2.G, R9.Pin_0
  N33: Q2.D, FAN.pin1
  N34: Q2.S, R10.Pin_0
